// Logisim project d_i-ne.circ as structural Verilog: 1 circuit, main circuit main
module main (
  input  D,
  input  C
);

  wire nand_1_out, nand_2_out, nand_3_out, nand_4_out, nand_5_out;

  nand nand_1 (nand_1_out, D, D);
  nand nand_2 (nand_2_out, D, C);
  nand nand_3 (nand_3_out, C, nand_1_out);
  nand nand_4 (nand_4_out, nand_2_out, nand_5_out);
  nand nand_5 (nand_5_out, nand_4_out, nand_3_out);
  LED led_1 (.in(nand_4_out));
  LED led_2 (.in(nand_5_out));

  // Notes on the sheet:
  //   Q
  //   not Q
endmodule
