// Logisim project jk.circ as structural Verilog: 1 circuit, main circuit main
module main (
  input  not_S,
  input  J,
  input  K,
  input  not_R
);

  wire clock_1_out, nand_1_out, nand_2_out, nand_3_out, nand_4_out, nand_5_out, nand_6_out, nand_7_out,
       nand_8_out;

  Clock clock_1 (.out(clock_1_out));
  nand nand_1 (nand_1_out, nand_8_out, J, clock_1_out);
  nand nand_2 (nand_2_out, clock_1_out, K, nand_7_out);
  nand nand_3 (nand_3_out, not_S, nand_1_out, nand_4_out);
  nand nand_4 (nand_4_out, nand_3_out, nand_2_out, not_R);
  nand nand_5 (nand_5_out, nand_3_out, nand_1_out, nand_2_out);
  nand nand_6 (nand_6_out, nand_2_out, nand_1_out, nand_4_out);
  nand nand_7 (nand_7_out, not_S, nand_8_out, nand_5_out);
  nand nand_8 (nand_8_out, nand_6_out, nand_7_out, not_R);
  LED led_1 (.in(nand_7_out));
  LED led_2 (.in(nand_8_out));

  // Notes on the sheet:
  //   C
  //   Q
  //   not Q
endmodule
