// Logisim project rs_i-ne.circ as structural Verilog: 1 circuit, main circuit main
module main (
  input  not_S,
  input  not_R
);

  wire clock_1_out, nand_1_out, nand_2_out, nand_3_out, nand_4_out, nand_5_out, nand_6_out;

  Clock clock_1 (.out(clock_1_out));
  nand nand_1 (nand_1_out, not_S, nand_3_out);
  nand nand_2 (nand_2_out, nand_4_out, not_R);
  nand nand_3 (nand_3_out, nand_4_out, nand_1_out, clock_1_out);
  nand nand_4 (nand_4_out, clock_1_out, nand_2_out, nand_3_out);
  nand nand_5 (nand_5_out, nand_3_out, nand_6_out);
  nand nand_6 (nand_6_out, nand_5_out, nand_4_out);
  LED led_1 (.in(nand_5_out));
  LED led_2 (.in(nand_6_out));

  // Notes on the sheet:
  //   C
  //   Q
  //   not Q
endmodule
