// Logisim project rs_ili-ne.circ as structural Verilog: 1 circuit, main circuit main
module main (
  input  not_S,
  input  not_R
);

  wire clock_1_out, nor_1_out, nor_2_out, nor_3_out, nor_4_out, nor_5_out, nor_6_out;

  Clock clock_1 (.out(clock_1_out));
  nor nor_1 (nor_1_out, not_S, nor_3_out);
  nor nor_2 (nor_2_out, nor_4_out, not_R);
  nor nor_3 (nor_3_out, nor_4_out, nor_1_out, clock_1_out);
  nor nor_4 (nor_4_out, clock_1_out, nor_2_out, nor_3_out);
  nor nor_5 (nor_5_out, nor_3_out, nor_6_out);
  nor nor_6 (nor_6_out, nor_5_out, nor_4_out);
  LED led_1 (.in(nor_5_out));
  LED led_2 (.in(nor_6_out));

  // Notes on the sheet:
  //   C
  //   Q
  //   not Q
endmodule
