// Logisim project s_rs-i-ne_2.circ as structural Verilog: 1 circuit, main circuit main
module main (
  input  not_S,
  input  S,
  input  R,
  input  not_R
);

  wire clock_1_out, nand_1_out, nand_2_out, nand_3_out, nand_4_out, nand_5_out, nand_6_out, nand_7_out,
       nand_8_out, nand_9_out;

  Clock clock_1 (.out(clock_1_out));
  nand nand_1 (nand_1_out, clock_1_out, clock_1_out);
  nand nand_2 (nand_2_out, S, nand_1_out);
  nand nand_3 (nand_3_out, nand_1_out, R);
  nand nand_4 (nand_4_out, not_S, nand_2_out, nand_5_out);
  nand nand_5 (nand_5_out, nand_4_out, nand_3_out, not_R);
  nand nand_6 (nand_6_out, nand_4_out, clock_1_out);
  nand nand_7 (nand_7_out, clock_1_out, nand_5_out);
  nand nand_8 (nand_8_out, not_S, nand_6_out, nand_9_out);
  LED led_1 (.in(nand_8_out));
  LED led_2 (.in(nand_9_out));
  nand nand_9 (nand_9_out, nand_8_out, nand_7_out, not_R);

  // Notes on the sheet:
  //   C
  //   Q
  //   not Q
endmodule
