// Logisim project s_rs_i-ne.circ as structural Verilog: 1 circuit, main circuit main
module main (
  input  S,
  input  C,
  input  R
);

  wire nand_1_out, nand_2_out, nand_3_out, nand_4_out;

  nand nand_1 (nand_1_out, S, C);
  nand nand_2 (nand_2_out, C, R);
  nand nand_3 (nand_3_out, nand_1_out, nand_4_out);
  nand nand_4 (nand_4_out, nand_3_out, nand_2_out);
  LED led_1 (.in(nand_3_out));
  LED led_2 (.in(nand_4_out));

  // Notes on the sheet:
  //   Q
  //   not Q
endmodule
